// Logisim project 8-bit-computer.circ as structural Verilog: 1 circuit, main circuit main
module main (
  input  PC_in,
  input  PC_write,
  input  IR_in,
  input  MEM_out,
  input  in_5,
  input  in_6,
  input  in_7,
  input  in_8,
  input  in_9,
  input  in_10,
  input  in_11,
  input  in_12,
  input  OUT_in,
  input  Signed,
  output out_15,
  output out_16,
  output out_17,
  output out_18,
  output out_19,
  output out_20,
  output out_21,
  output out_22
);

  wire and_1_out, and_2_out, and_3_out, and_4_out, and_5_out, and_6_out, and_7_out, and_8_out, and_9_out,
       and_10_out, and_11_out, and_12_out, and_13_out, and_14_out, and_15_out, and_16_out, and_17_out,
       and_18_out, and_19_out, and_20_out, and_21_out, and_22_out, and_23_out, and_24_out, and_25_out,
       and_26_out, and_27_out, and_28_out, and_29_out, and_30_out, and_31_out, and_32_out, Clock_out,
       not_1_out, not_2_out, not_3_out, not_4_out, not_5_out, not_6_out, not_7_out, not_8_out, not_9_out,
       not_10_out, not_11_out, not_12_out, or_1_out, or_3_out, or_4_out, or_6_out, or_7_out, or_9_out,
       or_10_out, or_12_out, or_13_out, or_15_out, or_16_out, or_18_out, or_19_out, or_21_out, or_22_out,
       or_24_out, or_25_out, or_26_out, or_27_out, or_28_out, or_29_out, or_30_out, or_31_out, or_32_out,
       or_33_out, or_34_out, or_35_out, or_36_out, or_37_out, or_38_out, or_39_out, or_40_out, or_41_out,
       or_42_out, or_43_out, or_44_out, or_45_out, or_46_out, or_47_out, or_48_out, or_49_out, or_50_out,
       or_51_out, or_52_out, or_53_out, or_54_out, or_55_out, or_56_out, or_57_out, or_58_out, or_59_out,
       or_60_out, or_61_out, or_62_out, or_63_out, or_64_out, xor_1_out, xor_2_out, xor_3_out, xor_4_out,
       xor_5_out, xor_6_out, xor_7_out, xor_8_out, xor_9_out, xor_10_out;
  wire [7:0] register_13_q, register_21_q, rom_1_data, rom_2_data, rom_3_data, rom_4_data, rom_5_data,
       rom_6_data, rom_7_data, rom_8_data;
  wire [11:0] register_1_q;

  not not_1 (not_1_out, Clock_out);
  Clock Clock (.out(Clock_out));
  Register #(.width(1)) register_1 (.D(not_3_out), .en(1'b1), .Q(register_1_q[0]), .clk(Clock_out));  // open: clr
  Register #(.width(1)) register_2 (.D(xor_1_out), .en(1'b1), .Q(register_1_q[1]), .clk(Clock_out));  // open: clr
  Register #(.width(1)) register_3 (.D(xor_2_out), .en(1'b1), .Q(register_1_q[2]), .clk(Clock_out));  // open: clr
  Register #(.width(1)) register_4 (.D(xor_3_out), .en(1'b1), .Q(register_1_q[3]), .clk(Clock_out));  // open: clr
  not not_2 (not_2_out, Clock_out);
  Register #(.width(1)) register_5 (.D(out_22), .en(IR_in), .Q(register_1_q[4]), .clk(not_2_out));  // open: clr
  Register #(.width(1)) register_6 (.D(out_21), .en(IR_in), .Q(register_1_q[5]), .clk(not_2_out));  // open: clr
  Register #(.width(1)) register_7 (.D(out_20), .en(IR_in), .Q(register_1_q[6]), .clk(not_2_out));  // open: clr
  Register #(.width(1)) register_8 (.D(out_19), .en(IR_in), .Q(register_1_q[7]), .clk(not_2_out));  // open: clr
  Register #(.width(1)) register_9 (.D(out_18), .en(IR_in), .Q(register_1_q[8]), .clk(not_2_out));  // open: clr
  Register #(.width(1)) register_10 (.D(out_17), .en(IR_in), .Q(register_1_q[9]), .clk(not_2_out));  // open: clr
  Register #(.width(1)) register_11 (.D(out_16), .en(IR_in), .Q(register_1_q[10]), .clk(not_2_out));  // open: clr
  Register #(.width(1)) register_12 (.D(out_15), .en(IR_in), .Q(register_1_q[11]), .clk(not_2_out));  // open: clr
  not not_3 (not_3_out, register_1_q[0]);
  and and_1 (and_1_out, register_1_q[0], register_1_q[1]);
  and and_2 (and_2_out, and_1_out, register_1_q[2]);
  xor xor_1 (xor_1_out, register_1_q[0], register_1_q[1]);
  xor xor_2 (xor_2_out, and_1_out, register_1_q[2]);
  xor xor_3 (xor_3_out, and_2_out, register_1_q[3]);
  ROM #(.addrWidth(14)) rom_1 (.addr({2'b00, register_1_q}), .data(rom_1_data));  // open: sel
  ROM #(.addrWidth(14)) rom_2 (.addr({2'b01, register_1_q}), .data(rom_2_data));  // open: sel
  ROM #(.addrWidth(14)) rom_3 (.addr({2'b10, register_1_q}), .data(rom_3_data));  // open: sel
  ROM #(.addrWidth(14)) rom_4 (.addr({2'b11, register_1_q}), .data(rom_4_data));  // open: sel
  or or_1 (or_1_out, or_25_out, or_26_out);
  or or_2 (out_22, or_1_out, or_3_out);
  or or_3 (or_3_out, or_27_out, or_28_out);
  or or_4 (or_4_out, or_29_out, or_30_out);
  or or_5 (out_21, or_4_out, or_6_out);
  or or_6 (or_6_out, or_31_out, or_32_out);
  or or_7 (or_7_out, or_33_out, or_34_out);
  or or_8 (out_20, or_7_out, or_9_out);
  or or_9 (or_9_out, or_35_out, or_36_out);
  or or_10 (or_10_out, or_37_out, or_38_out);
  or or_11 (out_19, or_10_out, or_12_out);
  or or_12 (or_12_out, or_39_out, or_40_out);
  or or_13 (or_13_out, or_41_out, or_42_out);
  or or_14 (out_18, or_13_out, or_15_out);
  or or_15 (or_15_out, or_43_out, or_44_out);
  or or_16 (or_16_out, or_45_out, or_46_out);
  or or_17 (out_17, or_16_out, or_18_out);
  or or_18 (or_18_out, or_47_out, or_48_out);
  or or_19 (or_19_out, or_49_out, or_50_out);
  or or_20 (out_16, or_19_out, or_21_out);
  or or_21 (or_21_out, or_51_out, or_52_out);
  or or_22 (or_22_out, or_53_out, or_54_out);
  or or_23 (out_15, or_22_out, or_24_out);
  or or_24 (or_24_out, or_55_out, or_56_out);
  or or_25 (or_25_out, and_19_out, 1'b0);
  or or_26 (or_26_out, 1'b0, 1'b0);
  or or_27 (or_27_out, 1'b0, 1'b0);
  or or_28 (or_28_out, 1'b0, in_12);
  or or_29 (or_29_out, and_20_out, 1'b0);
  or or_30 (or_30_out, 1'b0, 1'b0);
  or or_31 (or_31_out, 1'b0, 1'b0);
  or or_32 (or_32_out, 1'b0, in_11);
  or or_33 (or_33_out, and_21_out, 1'b0);
  or or_34 (or_34_out, 1'b0, 1'b0);
  or or_35 (or_35_out, 1'b0, 1'b0);
  or or_36 (or_36_out, 1'b0, in_10);
  or or_37 (or_37_out, and_22_out, 1'b0);
  or or_38 (or_38_out, 1'b0, 1'b0);
  or or_39 (or_39_out, 1'b0, 1'b0);
  or or_40 (or_40_out, 1'b0, in_9);
  or or_41 (or_41_out, and_23_out, 1'b0);
  or or_42 (or_42_out, 1'b0, 1'b0);
  or or_43 (or_43_out, 1'b0, 1'b0);
  or or_44 (or_44_out, 1'b0, in_8);
  or or_45 (or_45_out, and_24_out, 1'b0);
  or or_46 (or_46_out, 1'b0, 1'b0);
  or or_47 (or_47_out, 1'b0, 1'b0);
  or or_48 (or_48_out, 1'b0, in_7);
  or or_49 (or_49_out, and_25_out, 1'b0);
  or or_50 (or_50_out, 1'b0, 1'b0);
  or or_51 (or_51_out, 1'b0, 1'b0);
  or or_52 (or_52_out, 1'b0, in_6);
  or or_53 (or_53_out, and_26_out, 1'b0);
  or or_54 (or_54_out, 1'b0, 1'b0);
  or or_55 (or_55_out, 1'b0, 1'b0);
  or or_56 (or_56_out, 1'b0, in_5);
  Register #(.width(1)) register_13 (.D(out_22), .en(OUT_in), .Q(register_13_q[0]), .clk(not_1_out));  // open: clr
  Register #(.width(1)) register_14 (.D(out_21), .en(OUT_in), .Q(register_13_q[1]), .clk(not_1_out));  // open: clr
  Register #(.width(1)) register_15 (.D(out_20), .en(OUT_in), .Q(register_13_q[2]), .clk(not_1_out));  // open: clr
  Register #(.width(1)) register_16 (.D(out_19), .en(OUT_in), .Q(register_13_q[3]), .clk(not_1_out));  // open: clr
  Register #(.width(1)) register_17 (.D(out_18), .en(OUT_in), .Q(register_13_q[4]), .clk(not_1_out));  // open: clr
  Register #(.width(1)) register_18 (.D(out_17), .en(OUT_in), .Q(register_13_q[5]), .clk(not_1_out));  // open: clr
  Register #(.width(1)) register_19 (.D(out_16), .en(OUT_in), .Q(register_13_q[6]), .clk(not_1_out));  // open: clr
  Register #(.width(1)) register_20 (.D(out_15), .en(OUT_in), .Q(register_13_q[7]), .clk(not_1_out));  // open: clr
  and and_3 (and_3_out, not_12_out, not_4_out);
  not not_4 (not_4_out, PC_write);
  and and_4 (and_4_out, PC_write, out_22);
  and and_5 (and_5_out, xor_4_out, not_5_out);
  not not_5 (not_5_out, PC_write);
  and and_6 (and_6_out, PC_write, out_21);
  and and_7 (and_7_out, xor_5_out, not_6_out);
  not not_6 (not_6_out, PC_write);
  and and_8 (and_8_out, PC_write, out_20);
  and and_9 (and_9_out, xor_6_out, not_7_out);
  not not_7 (not_7_out, PC_write);
  and and_10 (and_10_out, PC_write, out_19);
  and and_11 (and_11_out, xor_7_out, not_8_out);
  not not_8 (not_8_out, PC_write);
  and and_12 (and_12_out, PC_write, out_18);
  and and_13 (and_13_out, xor_8_out, not_9_out);
  not not_9 (not_9_out, PC_write);
  and and_14 (and_14_out, PC_write, out_17);
  and and_15 (and_15_out, xor_9_out, not_10_out);
  not not_10 (not_10_out, PC_write);
  and and_16 (and_16_out, PC_write, out_16);
  and and_17 (and_17_out, xor_10_out, not_11_out);
  not not_11 (not_11_out, PC_write);
  and and_18 (and_18_out, PC_write, out_15);
  and and_19 (and_19_out, MEM_out, rom_5_data[0]);
  and and_20 (and_20_out, MEM_out, rom_5_data[1]);
  and and_21 (and_21_out, MEM_out, rom_5_data[2]);
  and and_22 (and_22_out, MEM_out, rom_5_data[3]);
  and and_23 (and_23_out, MEM_out, rom_5_data[4]);
  and and_24 (and_24_out, MEM_out, rom_5_data[5]);
  and and_25 (and_25_out, MEM_out, rom_5_data[6]);
  and and_26 (and_26_out, MEM_out, rom_5_data[7]);
  or or_57 (or_57_out, and_3_out, and_4_out);
  or or_58 (or_58_out, and_5_out, and_6_out);
  or or_59 (or_59_out, and_7_out, and_8_out);
  or or_60 (or_60_out, and_9_out, and_10_out);
  or or_61 (or_61_out, and_11_out, and_12_out);
  or or_62 (or_62_out, and_13_out, and_14_out);
  or or_63 (or_63_out, and_15_out, and_16_out);
  or or_64 (or_64_out, and_17_out, and_18_out);
  ROM rom_5 (.addr(register_21_q), .data(rom_5_data));  // open: sel
  Register #(.width(1)) register_21 (.D(or_57_out), .en(PC_in), .Q(register_21_q[0]), .clk(not_1_out));  // open: clr
  Register #(.width(1)) register_22 (.D(or_58_out), .en(PC_in), .Q(register_21_q[1]), .clk(not_1_out));  // open: clr
  Register #(.width(1)) register_23 (.D(or_59_out), .en(PC_in), .Q(register_21_q[2]), .clk(not_1_out));  // open: clr
  Register #(.width(1)) register_24 (.D(or_60_out), .en(PC_in), .Q(register_21_q[3]), .clk(not_1_out));  // open: clr
  Register #(.width(1)) register_25 (.D(or_61_out), .en(PC_in), .Q(register_21_q[4]), .clk(not_1_out));  // open: clr
  Register #(.width(1)) register_26 (.D(or_62_out), .en(PC_in), .Q(register_21_q[5]), .clk(not_1_out));  // open: clr
  Register #(.width(1)) register_27 (.D(or_63_out), .en(PC_in), .Q(register_21_q[6]), .clk(not_1_out));  // open: clr
  Register #(.width(1)) register_28 (.D(or_64_out), .en(PC_in), .Q(register_21_q[7]), .clk(not_1_out));  // open: clr
  ROM #(.addrWidth(9)) rom_6 (.addr({Signed, register_13_q}), .data(rom_6_data));  // open: sel
  ROM #(.addrWidth(9)) rom_7 (.addr({Signed, register_13_q}), .data(rom_7_data));  // open: sel
  ROM #(.addrWidth(9)) rom_8 (.addr({Signed, register_13_q}), .data(rom_8_data));  // open: sel
  not not_12 (not_12_out, register_21_q[0]);
  xor xor_4 (xor_4_out, register_21_q[0], register_21_q[1]);
  and and_27 (and_27_out, register_21_q[0], register_21_q[1]);
  xor xor_5 (xor_5_out, and_27_out, register_21_q[2]);
  and and_28 (and_28_out, and_27_out, register_21_q[2]);
  xor xor_6 (xor_6_out, and_28_out, register_21_q[3]);
  and and_29 (and_29_out, and_28_out, register_21_q[3]);
  xor xor_7 (xor_7_out, and_29_out, register_21_q[4]);
  and and_30 (and_30_out, and_29_out, register_21_q[4]);
  xor xor_8 (xor_8_out, and_30_out, register_21_q[5]);
  and and_31 (and_31_out, and_30_out, register_21_q[5]);
  xor xor_9 (xor_9_out, and_31_out, register_21_q[6]);
  and and_32 (and_32_out, and_31_out, register_21_q[6]);
  xor xor_10 (xor_10_out, and_32_out, register_21_q[7]);
  DotMatrix #(.matrixcols(3), .matrixrows(1)) dotmatrix_1 (
    .col0(rom_6_data[7]), .col1(rom_6_data[7]), .col2(rom_6_data[7]));
  _7_Segment_Display u_7_segment_display_1 (
    .g(rom_6_data[3]), .f(rom_6_data[2]), .a(rom_6_data[1]), .b(rom_6_data[0]), .e(rom_6_data[4]),
    .d(rom_6_data[5]), .c(rom_6_data[6]));  // open: dp
  _7_Segment_Display u_7_segment_display_2 (
    .g(rom_7_data[3]), .f(rom_7_data[2]), .a(rom_7_data[1]), .b(rom_7_data[0]), .e(rom_7_data[4]),
    .d(rom_7_data[5]), .c(rom_7_data[6]));  // open: dp
  _7_Segment_Display u_7_segment_display_3 (
    .g(rom_8_data[3]), .f(rom_8_data[2]), .a(rom_8_data[1]), .b(rom_8_data[0]), .e(rom_8_data[4]),
    .d(rom_8_data[5]), .c(rom_8_data[6]));  // open: dp

  // Notes on the sheet:
  //   Manual Bus Override
endmodule
